# Fritzing sketch PeterPen (saved by Fritzing 0.9.3b)
breadboards: 1

parts:
  U1 = NodeMCU V1.0
  Componente1 = InvenSense MPU6050
  J1 = Basic Force Sensing Resistor (FSR) [package=THT]
  R1 = Resistor [tolerance=±5% resistance=10k package=THT]
  VCC1 = Battery block 9V
  R2 = Resistor [tolerance=±5% resistance=220 package="2512 [SMD]"]
  LED2 = smd LED [color="Red (633nm)" package="0805 [SMD]"]

nets:
  N1: U1.D1, Componente1.SCL
  N2: U1.D2, Componente1.SDA
  N3: U1.D3, R2.Pin_1
  3V3: U1.3V3, Componente1.VCC, J1.pin_0
  GND: U1.GND, Componente1.GND, Componente1.AD0, R1.Pin_1, VCC1.-, LED2.cathode
  N4: U1.Vin, VCC1.+
  N5: U1.A0, J1.pin_1, R1.Pin_0
  N6: R2.Pin_0, LED2.anode

custom parts:
  NodeMCU V1.0: ESP8266 based NodeMCU
